// Logisim project cpu.circ as structural Verilog: 1 circuit, main circuit main
module main (
  input  [31:0] INSTRUCTION,
  input  CLOCK,
  output [31:0] PROGRAM_COUNTER,
  output [31:0] ra,
  output [31:0] sp,
  output [31:0] t0,
  output [31:0] t1,
  output [31:0] t2,
  output [31:0] s0,
  output [31:0] s1,
  output [31:0] a0
);

  wire DMEM_p1, DMEM_p4;
  wire [2:0] func3;
  wire [4:0] rs2_In;
  wire [11:0] imm;
  wire [19:0] INSTRUCTION_OUT;
  wire [31:0] adder_1_out, ALU_Out, imm_Extended, multiplexer_1_out, rs1_Out, rs2_Out;

  Adder #(.width(32)) adder_1 (.a(PROGRAM_COUNTER), .b(32'h4), .out(adder_1_out));  // open: cin, cout
  Register #(.width(32)) register_1 (
    .D(INSTRUCTION), .clk(CLOCK), .Q({imm, INSTRUCTION_OUT[19:15], func3, INSTRUCTION_OUT[11:0]}));  // open: en, clr
  Register #(.width(32)) PC (.D(adder_1_out), .clk(CLOCK), .Q(PROGRAM_COUNTER));  // open: en, clr
  Bit_Extender #(.in_width(12), .out_width(32), .\type ("input")) bit_extender_1 (
    .in(imm), .out(imm_Extended));  // open: extend
  regfile_main RegFile (
    .rs2(rs2_In), .rd(INSTRUCTION_OUT[11:7]), .Read_Data_1(rs1_Out), .Read_Data_2(rs2_Out), .ra(ra), .sp(sp),
    .t0(t0), .t1(t1), .t2(t2), .s0(s0), .s1(s1), .a0(a0), .rs1(INSTRUCTION_OUT[19:15]), .Write_Data(ALU_Out),
    .RegWEn(1'b1), .clk(CLOCK));
  Multiplexer #(.width(32), .enable("false")) multiplexer_1 (
    .in0(rs2_Out), .in1(imm_Extended), .out(multiplexer_1_out), .sel(1'b1));
  alu Arithmetic_Logic_Unit (.B(multiplexer_1_out), .Result(ALU_Out), .A(rs1_Out), .ALUSel(4'b0000));
  // mem_main DMEM: pin names not known; wires that end beside it: DMEM_p1, DMEM_p1, CLOCK, DMEM_p4

  // Other names for the same wires on the sheet: clk = CLOCK; opcode[6:0] = INSTRUCTION_OUT[6:0];
  //   rd[4:0] = INSTRUCTION_OUT[11:7]; INSTRUCTION_OUT (some bits) = {imm, func3};
  //   rs1_In[4:0] = INSTRUCTION_OUT[19:15]

  // Notes on the sheet:
  //   Output
  //   IMEM (do **NOT** move this)
  //   Inputs
  //   Inputs/Outputs for testing. Do **NOT** move these.
endmodule
